// Logisim project part2.circ as structural Verilog: 1 circuit, main circuit my circuit
// First Tunnel
module my_circuit (
  input  [3:0] in_1,
  input  [1:0] in_2,
  input  [3:0] in_3,
  output [1:0] Output
);

  wire button_1_out, clock_1_out;
  wire [7:0] register_1_q;

  Register register_1 (.D({in_1, in_3}), .Q(register_1_q), .clk(clock_1_out), .clr(button_1_out));  // open: en
  Clock clock_1 (.out(clock_1_out));
  Button button_1 (.out(button_1_out));
  Multiplexer #(.select(2), .width(2), .disabled(0), .enable("false")) multiplexer_1 (
    .in0(register_1_q[1:0]), .in1(register_1_q[3:2]), .in2(register_1_q[5:4]), .in3(register_1_q[7:6]),
    .out(Output), .sel(in_2));

  // Other names for the same wires on the sheet: First_Tunnel[1:0] = Output

  // Notes on the sheet:
  //   Yuen Han Chan
endmodule
