// Logisim project HW3.circ as structural Verilog: 5 circuits, main circuit 16-bit ALU
// 1+
module _1_bit_Full_Adder (
  input  a,
  input  b,
  input  carry_in,
  output out_4,
  output out_5
);

  wire and_1_out, and_2_out, and_3_out, and_4_out, and_5_out, and_6_out, and_7_out, not_1_out, not_2_out,
       not_3_out, not_4_out, not_5_out, not_6_out, not_7_out, not_8_out, not_9_out;

  not not_1 (not_1_out, a);
  and and_1 (and_1_out, not_1_out, not_2_out, carry_in);
  not not_2 (not_2_out, b);
  not not_3 (not_3_out, a);
  and and_2 (and_2_out, not_3_out, b, not_4_out);
  not not_4 (not_4_out, carry_in);
  not not_5 (not_5_out, a);
  and and_3 (and_3_out, not_5_out, b, carry_in);
  and and_4 (and_4_out, a, not_6_out, not_7_out);
  not not_6 (not_6_out, b);
  not not_7 (not_7_out, carry_in);
  and and_5 (and_5_out, a, not_8_out, carry_in);
  not not_8 (not_8_out, b);
  and and_6 (and_6_out, a, b, not_9_out);
  not not_9 (not_9_out, carry_in);
  and and_7 (and_7_out, a, b, carry_in);
  or Answer (out_5, and_7_out, and_1_out, and_2_out, and_4_out);
  or Carry_Out (out_4, and_3_out, and_5_out, and_6_out, and_7_out);

  // Other names for the same wires on the sheet: Answer = out_5; Carry_Out = out_4

  // Notes on the sheet:
  //   Yuen Han Chan
  //   9/8/2014
  //   HW3
endmodule

// 4+
module _4_bit_Full_Adder (
  input  carry_in,
  input  [3:0] a,
  input  [3:0] b,
  output [3:0] out_4,
  output out_5
);

  wire n1_bit_full_adder_2_out_4, n1_bit_full_adder_3_out_4, n1_bit_full_adder_4_out_4;

  _1_bit_Full_Adder u_1_bit_full_adder_1 (
    .a(a[3]), .b(b[3]), .carry_in(n1_bit_full_adder_2_out_4), .out_4(out_5), .out_5(out_4[3]));
  _1_bit_Full_Adder u_1_bit_full_adder_2 (
    .a(a[2]), .b(b[2]), .carry_in(n1_bit_full_adder_4_out_4), .out_4(n1_bit_full_adder_2_out_4),
    .out_5(out_4[2]));
  _1_bit_Full_Adder u_1_bit_full_adder_3 (
    .a(a[0]), .b(b[0]), .carry_in(carry_in), .out_4(n1_bit_full_adder_3_out_4), .out_5(out_4[0]));
  _1_bit_Full_Adder u_1_bit_full_adder_4 (
    .a(a[1]), .b(b[1]), .carry_in(n1_bit_full_adder_3_out_4), .out_4(n1_bit_full_adder_4_out_4),
    .out_5(out_4[1]));

  // Other names for the same wires on the sheet: Answer[3:0] = out_4; Carry_out = out_5

  // Notes on the sheet:
  //   Yuen Han Chan
  //   9/8/2014
  //   HW3
endmodule

module _4_bit_ALU (
  input  [3:0] in_1,
  input  [3:0] in_2,
  input  in_3,
  input  M0,
  input  M2,
  input  M3,
  output carry_out,
  output out_8,
  output carry_out_2,
  output carry_out_3,
  output [3:0] out_11
);

  wire [3:0] AandB, Addition, AorB, AxorB, Increment, n4_bit_full_adder_2_out_4, Negation, not_2_out,
       Right_Shift, Subtraction;

  _4_bit_Full_Adder u_4_bit_full_adder_1 (.a(in_1), .b(in_2), .out_4(Addition), .carry_in(in_3), .out_5(carry_out));
  _4_bit_Full_Adder u_4_bit_full_adder_2 (
    .a(4'b0001), .b(not_2_out), .out_4(n4_bit_full_adder_2_out_4), .carry_in(in_3));  // open: out_5
  _4_bit_Full_Adder u_4_bit_full_adder_3 (
    .a(in_1), .b(n4_bit_full_adder_2_out_4), .out_4(Subtraction), .carry_in(in_3), .out_5(carry_out_2));
  _4_bit_Full_Adder u_4_bit_full_adder_4 (
    .a(in_1), .b(4'b0001), .out_4(Increment), .carry_in(in_3), .out_5(carry_out_3));
  assign Negation = ~in_1;  // NOT_Gate not_1, 4 bits wide
  assign not_2_out = ~in_2;  // NOT_Gate not_2, 4 bits wide
  assign Right_Shift = {{1{1'b0}}, in_1[3:1]};  // Bit_Extender bit_extender_1
  Multiplexer #(.select(3), .width(4), .disabled(0), .enable("false")) multiplexer_1 (
    .in0(Addition), .in1(Subtraction), .in2(Increment), .in3(Negation), .in4(Right_Shift), .in5(AandB),
    .in6(AorB), .in7(AxorB), .out(out_11), .sel({M3, M2, M0}));
  assign AandB = in_1 & in_2;  // AND_Gate and_1, 4 bits wide
  assign AorB = in_1 | in_2;  // OR_Gate or_1, 4 bits wide
  assign AxorB = in_1 ^ in_2;  // XOR_Gate xor_1, 4 bits wide

  assign out_8 = in_1[0];

  // Other names for the same wires on the sheet: a[3:0] = in_1; b[3:0] = in_2; Carry_in = in_3

  // Notes on the sheet:
  //   Addition
  //   Subtraction
  //   Increment
  //   Negation
  //   Right Shift 1
  //   100
  //   000
  //   001
  //   110
  //   010
  //   A and B
  //   101
  //   011
  //   A or B
  //   111
  //   Yuen Han Chan
  //   9/8/2014
  //   HW3
  //   Op-Code
  //   A + B 000
  //   A - B 100
  //   A + 1 010
  //   -A  110
  //   A >> 1 001
  //   A & B 101
  //   A|B 011
  //   A^B 111
endmodule

// 16+
module _16_bit_Full_Adder (
  input  carry_in,
  input  [15:0] a,
  input  [15:0] b,
  output [15:0] out_4,
  output out_5
);

  wire n4_bit_full_adder_1_out_5, n4_bit_full_adder_2_out_5, n4_bit_full_adder_3_out_5;

  _4_bit_Full_Adder u_4_bit_full_adder_1 (
    .a(a[3:0]), .b(b[3:0]), .out_4(out_4[3:0]), .carry_in(carry_in), .out_5(n4_bit_full_adder_1_out_5));
  _4_bit_Full_Adder u_4_bit_full_adder_2 (
    .a(a[7:4]), .b(b[7:4]), .out_4(out_4[7:4]), .carry_in(n4_bit_full_adder_1_out_5),
    .out_5(n4_bit_full_adder_2_out_5));
  _4_bit_Full_Adder u_4_bit_full_adder_3 (
    .a(a[11:8]), .b(b[11:8]), .out_4(out_4[11:8]), .carry_in(n4_bit_full_adder_2_out_5),
    .out_5(n4_bit_full_adder_3_out_5));
  _4_bit_Full_Adder u_4_bit_full_adder_4 (
    .a(a[15:12]), .b(b[15:12]), .out_4(out_4[15:12]), .carry_in(n4_bit_full_adder_3_out_5), .out_5(out_5));

  // Other names for the same wires on the sheet: Answer[15:0] = out_4; Carry_out = out_5

  // Notes on the sheet:
  //   Yuen Han Chan
  //   9/8/2014
  //   HW3
endmodule

module _16_bit_ALU (
  input  [15:0] in_1,
  input  [15:0] in_2,
  input  in_3,
  input  M0,
  input  M2,
  input  M3,
  output out_7,
  output carry_out,
  output carry_out_2,
  output carry_out_3,
  output [15:0] out_11
);

  wire [15:0] AandB, Addition, AorB, AxorB, Increment, n16_bit_full_adder_1_out_4, Negation, not_1_out,
       Right_Shift, Subtraction;

  _16_bit_Full_Adder u_16_bit_full_adder_1 (
    .carry_in(1'b0), .a(not_1_out), .b(16'h1), .out_4(n16_bit_full_adder_1_out_4));  // open: out_5
  assign not_1_out = ~in_2;  // NOT_Gate not_1, 16 bits wide
  assign Negation = ~in_1;  // NOT_Gate not_2, 16 bits wide
  _16_bit_Full_Adder u_16_bit_full_adder_2 (.carry_in(in_3), .a(in_1), .b(in_2), .out_4(Addition), .out_5(carry_out));
  _16_bit_Full_Adder u_16_bit_full_adder_3 (
    .carry_in(in_3), .a(in_1), .b(n16_bit_full_adder_1_out_4), .out_4(Subtraction), .out_5(carry_out_2));
  _16_bit_Full_Adder u_16_bit_full_adder_4 (
    .carry_in(in_3), .a(in_1), .b(16'h1), .out_4(Increment), .out_5(carry_out_3));
  assign Right_Shift = {{1{1'b0}}, in_1[15:1]};  // Bit_Extender bit_extender_1
  Multiplexer #(.select(3), .width(16), .disabled(0), .enable("false")) multiplexer_1 (
    .in0(Addition), .in1(Subtraction), .in2(Increment), .in3(Negation), .in4(Right_Shift), .in5(AandB),
    .in6(AorB), .in7(AxorB), .out(out_11), .sel({M3, M2, M0}));
  assign AandB = in_1 & in_2;  // AND_Gate and_1, 16 bits wide
  assign AorB = in_1 | in_2;  // OR_Gate or_1, 16 bits wide
  assign AxorB = in_1 ^ in_2;  // XOR_Gate xor_1, 16 bits wide

  assign out_7 = in_1[0];

  // Other names for the same wires on the sheet: a[15:0] = in_1; b[15:0] = in_2; Carry_in = in_3

  // Notes on the sheet:
  //   Addition
  //   Subtraction
  //   Increment
  //   Negation
  //   Right Shift 1
  //   100
  //   000
  //   001
  //   110
  //   010
  //   A and B
  //   101
  //   011
  //   A or B
  //   111
  //   Yuen Han Chan
  //   9/8/2014
  //   HW3
  //   Op-Code
  //   A + B 000
  //   A - B 100
  //   A + 1 010
  //   -A  110
  //   A >> 1 001
  //   A & B 101
  //   A|B 011
  //   A^B 111
endmodule
