// Logisim project hw4part2.circ as structural Verilog: 2 circuits, main circuit One-Hot State Machine
module Tester (
  input  G
);

  wire Clock_out, one_hot_state_machine_1_w, one_hot_state_machine_1_x, one_hot_state_machine_1_y,
       one_hot_state_machine_1_z, Reset_out;

  One_Hot_State_Machine one_hot_state_machine_1 (
    .W(one_hot_state_machine_1_w), .Clock(Clock_out), .Reset(Reset_out), .G(G),
    .X(one_hot_state_machine_1_x), .Y(one_hot_state_machine_1_y), .Z(one_hot_state_machine_1_z));
  Clock Clock (.out(Clock_out));
  LED W (.in(one_hot_state_machine_1_w));
  LED X (.in(one_hot_state_machine_1_x));
  LED Y (.in(one_hot_state_machine_1_y));
  LED Z (.in(one_hot_state_machine_1_z));
  Button Reset (.out(Reset_out));

  // Notes on the sheet:
  //   You can use this to test your circuit.
endmodule

module One_Hot_State_Machine (
  input  G,
  input  Clock,
  input  Reset,
  output W,
  output X,
  output Y,
  output Z
);

  wire and_3_out, and_4_out, and_6_out, and_7_out, and_8_out, and_9_out, and_10_out, N0, N1, N2, N3, N4, N5,
       N6, nor_1_out, not_1_out, not_2_out, not_3_out, not_4_out, not_5_out, S0, S1, S2, S3, S4, S5, S6;

  not not_1 (not_1_out, G);
  not not_2 (not_2_out, G);
  and and_1 (N1, G, S0);
  not not_3 (not_3_out, G);
  and and_2 (N2, not_3_out, S1);
  and and_3 (and_3_out, not_1_out, S4);
  and and_4 (and_4_out, not_2_out, S3);
  and and_5 (N4, G, S1);
  and and_6 (and_6_out, G, S3);
  and and_7 (and_7_out, G, S4);
  or or_1 (N6, S5, and_8_out);
  and and_8 (and_8_out, G, S6);
  or or_2 (N3, S2, and_3_out, and_4_out);
  or or_3 (N5, and_6_out, and_7_out);
  not not_4 (not_4_out, G);
  and and_9 (and_9_out, not_4_out, S0);
  not not_5 (not_5_out, G);
  and and_10 (and_10_out, not_5_out, S6);
  nor nor_1 (nor_1_out, S0, S1, S2, S3, S4, S5, S6);
  or or_4 (N0, and_9_out, and_10_out, nor_1_out);
  Register #(.width(7)) register_1 (
    .D({N6, N5, N4, N3, N2, N1, N0}), .Q({S6, S5, S4, S3, S2, S1, S0}), .clk(Clock), .clr(Reset));  // open: en
  or or_5 (W, S2, S3, S6);
  or or_6 (X, S0, S3);
  or or_7 (Y, S5, S3, S6);
  or or_8 (Z, S5, S2, S4);

  // Other names for the same wires on the sheet: CLK = Clock; RST = Reset

  // Notes on the sheet:
  //   My name is
  //   Yuen Han Chan
  //   and this is my pretty one-hot state machine!
endmodule
